// Logisim project bit32.circ as structural Verilog: 1 circuit, main circuit main
module main (
  input  [3:0] in_1,
  input  \int ,
  input  short,
  input  [3:0] in_4,
  input  in_5,
  output [31:0] out_6,
  output [31:0] out_7
);

  wire and_1_out, and_2_out, and_3_out, and_4_out, and_5_out, and_6_out, and_7_out, and_8_out, and_9_out,
       and_10_out, and_11_out, and_12_out, and_13_out, and_14_out, and_15_out, and_16_out, button_1_out,
       clock_1_out, demultiplexer_1_out0, demultiplexer_1_out1, demultiplexer_1_out2, demultiplexer_1_out3,
       demultiplexer_1_out4, demultiplexer_1_out5, demultiplexer_1_out6, demultiplexer_1_out7,
       demultiplexer_1_out8, demultiplexer_1_out9, demultiplexer_1_out10, demultiplexer_1_out11,
       demultiplexer_1_out12, demultiplexer_1_out13, demultiplexer_1_out14, demultiplexer_1_out15, or_1_out;
  wire [7:0] controlled_buffer_3_out, controlled_buffer_5_out, register_3_q, register_4_q, register_9_q,
       register_10_q, register_15_q, register_16_q, register_21_q, register_22_q;
  wire [15:0] controlled_buffer_4_out, controlled_buffer_6_out, r0_q, r1_q, register_2_q, register_5_q,
       register_7_q, register_8_q, register_11_q, register_13_q, register_14_q, register_17_q, register_18_q,
       register_20_q;
  wire [31:0] f0_q, f1_q, f2_q, f3_q, fp_q, lr_q, multiplexer_2_out, multiplexer_3_out, pc_q, sp_q, undriven;
  wire [31:8] multiplexer_1_out;

  Demultiplexer #(.select(4)) demultiplexer_1 (
    .out0(demultiplexer_1_out0), .out1(demultiplexer_1_out1), .out2(demultiplexer_1_out2),
    .out3(demultiplexer_1_out3), .out4(demultiplexer_1_out4), .out5(demultiplexer_1_out5),
    .out6(demultiplexer_1_out6), .out7(demultiplexer_1_out7), .out8(demultiplexer_1_out8),
    .out9(demultiplexer_1_out9), .out10(demultiplexer_1_out10), .out11(demultiplexer_1_out11),
    .out12(demultiplexer_1_out12), .out13(demultiplexer_1_out13), .out14(demultiplexer_1_out14),
    .out15(demultiplexer_1_out15), .in(in_5), .sel(in_4));
  or or_1 (or_1_out, \int , short);
  and and_1 (and_1_out, \int , demultiplexer_1_out0);
  and and_2 (and_2_out, or_1_out, demultiplexer_1_out0);
  and and_3 (and_3_out, \int , demultiplexer_1_out1);
  and and_4 (and_4_out, or_1_out, demultiplexer_1_out1);
  Register #(.width(16)) r0 (.D(undriven[31:16]), .en(and_1_out), .clk(clock_1_out), .Q(r0_q), .clr(button_1_out));
  Register register_1 (
    .D(undriven[15:8]), .en(and_2_out), .clk(clock_1_out), .Q(register_2_q[15:8]), .clr(button_1_out));
  Register register_2 (
    .D(undriven[7:0]), .en(demultiplexer_1_out0), .clk(clock_1_out), .Q(register_2_q[7:0]), .clr(button_1_out));
  Register #(.width(16)) r1 (.D(undriven[31:16]), .en(and_3_out), .clk(clock_1_out), .Q(r1_q), .clr(button_1_out));
  Register register_3 (.D(undriven[15:8]), .en(and_4_out), .clk(clock_1_out), .Q(register_3_q), .clr(button_1_out));
  Register register_4 (
    .D(undriven[7:0]), .en(demultiplexer_1_out1), .clk(clock_1_out), .Q(register_4_q), .clr(button_1_out));
  and and_5 (and_5_out, \int , demultiplexer_1_out2);
  and and_6 (and_6_out, or_1_out, demultiplexer_1_out2);
  and and_7 (and_7_out, \int , demultiplexer_1_out3);
  and and_8 (and_8_out, or_1_out, demultiplexer_1_out3);
  Register #(.width(16)) register_5 (
    .D(undriven[31:16]), .en(and_5_out), .clk(clock_1_out), .Q(register_5_q), .clr(button_1_out));
  Register register_6 (
    .D(undriven[15:8]), .en(and_6_out), .clk(clock_1_out), .Q(register_7_q[15:8]), .clr(button_1_out));
  Register register_7 (
    .D(undriven[7:0]), .en(demultiplexer_1_out2), .clk(clock_1_out), .Q(register_7_q[7:0]), .clr(button_1_out));
  Register #(.width(16)) register_8 (
    .D(undriven[31:16]), .en(and_7_out), .clk(clock_1_out), .Q(register_8_q), .clr(button_1_out));
  Register register_9 (.D(undriven[15:8]), .en(and_8_out), .clk(clock_1_out), .Q(register_9_q), .clr(button_1_out));
  Register register_10 (
    .D(undriven[7:0]), .en(demultiplexer_1_out3), .clk(clock_1_out), .Q(register_10_q), .clr(button_1_out));
  and and_9 (and_9_out, \int , demultiplexer_1_out4);
  and and_10 (and_10_out, or_1_out, demultiplexer_1_out4);
  and and_11 (and_11_out, \int , demultiplexer_1_out5);
  and and_12 (and_12_out, or_1_out, demultiplexer_1_out5);
  Register #(.width(16)) register_11 (
    .D(undriven[31:16]), .en(and_9_out), .clk(clock_1_out), .Q(register_11_q), .clr(button_1_out));
  Register register_12 (
    .D(undriven[15:8]), .en(and_10_out), .clk(clock_1_out), .Q(register_13_q[15:8]), .clr(button_1_out));
  Register register_13 (
    .D(undriven[7:0]), .en(demultiplexer_1_out4), .clk(clock_1_out), .Q(register_13_q[7:0]),
    .clr(button_1_out));
  Register #(.width(16)) register_14 (
    .D(undriven[31:16]), .en(and_11_out), .clk(clock_1_out), .Q(register_14_q), .clr(button_1_out));
  Register register_15 (.D(undriven[15:8]), .en(and_12_out), .clk(clock_1_out), .Q(register_15_q), .clr(button_1_out));
  Register register_16 (
    .D(undriven[7:0]), .en(demultiplexer_1_out5), .clk(clock_1_out), .Q(register_16_q), .clr(button_1_out));
  Register #(.width(16)) register_17 (
    .D(undriven[31:16]), .en(and_13_out), .clk(clock_1_out), .Q(register_17_q), .clr(button_1_out));
  and and_13 (and_13_out, \int , demultiplexer_1_out6);
  and and_14 (and_14_out, or_1_out, demultiplexer_1_out6);
  Register #(.width(16)) register_18 (
    .D(undriven[31:16]), .en(and_15_out), .clk(clock_1_out), .Q(register_18_q), .clr(button_1_out));
  and and_15 (and_15_out, \int , demultiplexer_1_out7);
  and and_16 (and_16_out, or_1_out, demultiplexer_1_out7);
  Register register_19 (
    .D(undriven[15:8]), .en(and_14_out), .clk(clock_1_out), .Q(register_20_q[15:8]), .clr(button_1_out));
  Register register_20 (
    .D(undriven[7:0]), .en(demultiplexer_1_out6), .clk(clock_1_out), .Q(register_20_q[7:0]),
    .clr(button_1_out));
  Register register_21 (.D(undriven[15:8]), .en(and_16_out), .clk(clock_1_out), .Q(register_21_q), .clr(button_1_out));
  Register register_22 (
    .D(undriven[7:0]), .en(demultiplexer_1_out7), .clk(clock_1_out), .Q(register_22_q), .clr(button_1_out));
  Clock clock_1 (.out(clock_1_out));
  Button button_1 (.out(button_1_out));
  Register #(.width(32)) f0 (.D(undriven), .en(demultiplexer_1_out8), .clk(clock_1_out), .Q(f0_q), .clr(button_1_out));
  Register #(.width(32)) f1 (.D(undriven), .en(demultiplexer_1_out9), .clk(clock_1_out), .Q(f1_q), .clr(button_1_out));
  Register #(.width(32)) f2 (.D(undriven), .en(demultiplexer_1_out10), .clk(clock_1_out), .Q(f2_q), .clr(button_1_out));
  Register #(.width(32)) f3 (.D(undriven), .en(demultiplexer_1_out11), .clk(clock_1_out), .Q(f3_q), .clr(button_1_out));
  Register #(.width(32)) lr (.D(undriven), .en(demultiplexer_1_out12), .clk(clock_1_out), .Q(lr_q), .clr(button_1_out));
  Register #(.width(32)) fp (.D(undriven), .en(demultiplexer_1_out13), .clk(clock_1_out), .Q(fp_q), .clr(button_1_out));
  Register #(.width(32)) sp (.D(undriven), .en(demultiplexer_1_out14), .clk(clock_1_out), .Q(sp_q), .clr(button_1_out));
  Register #(.width(32)) pc (.D(undriven), .en(demultiplexer_1_out15), .clk(clock_1_out), .Q(pc_q), .clr(button_1_out));
  Multiplexer #(.select(4), .width(32)) multiplexer_1 (
    .in0({r0_q, register_2_q}), .in1({r1_q, register_3_q, register_4_q}), .in2({register_5_q, register_7_q}),
    .in3({register_8_q, register_9_q, register_10_q}), .in4({register_11_q, register_13_q}),
    .in5({register_14_q, register_15_q, register_16_q}), .in6({register_17_q, register_20_q}),
    .in7({register_18_q, register_21_q, register_22_q}), .in8(f0_q), .in9(f1_q), .in10(f2_q), .in11(f3_q),
    .in12(lr_q), .in13(fp_q), .in14(sp_q), .in15(pc_q), .out({multiplexer_1_out, out_6[7:0]}), .sel(in_1));
  Multiplexer #(.select(4), .width(32)) multiplexer_2 (
    .in0({r0_q, register_2_q}), .in1({r1_q, register_3_q, register_4_q}), .in2({register_5_q, register_7_q}),
    .in3({register_8_q, register_9_q, register_10_q}), .in4({register_11_q, register_13_q}),
    .in5({register_14_q, register_15_q, register_16_q}), .in6({register_17_q, register_20_q}),
    .in7({register_18_q, register_21_q, register_22_q}), .in8(f0_q), .in9(f1_q), .in10(f2_q), .in11(f3_q),
    .in12(lr_q), .in13(fp_q), .in14(sp_q), .in15(pc_q), .out(multiplexer_2_out));  // open: sel
  Multiplexer #(.select(4), .width(32)) multiplexer_3 (
    .in0({r0_q, register_2_q}), .in1({r1_q, register_3_q, register_4_q}), .in2({register_5_q, register_7_q}),
    .in3({register_8_q, register_9_q, register_10_q}), .in4({register_11_q, register_13_q}),
    .in5({register_14_q, register_15_q, register_16_q}), .in6({register_17_q, register_20_q}),
    .in7({register_18_q, register_21_q, register_22_q}), .in8(f0_q), .in9(f1_q), .in10(f2_q), .in11(f3_q),
    .in12(lr_q), .in13(fp_q), .in14(sp_q), .in15(pc_q), .out(multiplexer_3_out));  // open: sel
  assign out_6[15:8] = or_1_out ? multiplexer_1_out[15:8] : 8'bz;  // Controlled_Buffer controlled_buffer_1
  assign out_6[31:16] = \int  ? multiplexer_1_out[31:16] : 16'bz;  // Controlled_Buffer controlled_buffer_2
  assign controlled_buffer_3_out = or_1_out ? multiplexer_2_out[15:8] : 8'bz;  // Controlled_Buffer controlled_buffer_3
  assign controlled_buffer_4_out = \int  ? multiplexer_2_out[31:16] : 16'bz;  // Controlled_Buffer controlled_buffer_4
  assign controlled_buffer_5_out = or_1_out ? multiplexer_3_out[15:8] : 8'bz;  // Controlled_Buffer controlled_buffer_5
  assign controlled_buffer_6_out = \int  ? multiplexer_3_out[31:16] : 16'bz;  // Controlled_Buffer controlled_buffer_6
  Adder #(.width(32)) adder_1 (.b(32'h1), .out(out_7));  // open: a, cin, cout
endmodule
